# Fritzing sketch activity3 (saved by Fritzing 0.8.7b)
breadboards: 1

parts:
  Part1 = Arduino Uno (Rev3)
  R1 = Resistor [tolerance=±5% resistance=1k package=THT]
  LED1 = smd LED [color="Red (635nm)" package="1206 [SMD]"]
  S1 = Pushbutton [package="[THT]"]

nets:
  N1: Part1.D11_PWM/MOSI, LED1.anode
  N2: Part1.D2, S1.Pin_3, S1.Pin_4
  N3: Part1.GND, R1.Pin_1, S1.Pin_1, S1.Pin_2
  N4: R1.Pin_0, LED1.cathode
