# Fritzing sketch activity4 (saved by Fritzing 0.9.1b)
breadboards: 1

parts:
  Part1 = Arduino Uno (Rev3)
  R1 = Resistor [tolerance=±5% resistance=1k package=THT]
  LED1 = RGB LED (com. anode, rbg) [package="5 mm [THT]"]
  S1 = Pushbutton [package="[SMD]"]
  R2 = Resistor [tolerance=±5% resistance=1k package=THT]
  R3 = Resistor [tolerance=±5% resistance=1k package=THT]

nets:
  N1: Part1.D9_PWM, R3.Pin_1
  N2: Part1.D10_PWM/SS, R2.Pin_1
  N3: Part1.D11_PWM/MOSI, R1.Pin_1
  N4: Part1.D2, S1.Pin_3, S1.Pin_4
  N5: Part1.5V, LED1.blue_cathode
  N6: Part1.GND, S1.Pin_1, S1.Pin_2
  N7: R1.Pin_0, LED1.red_cathode
  N8: LED1.common_anode, R2.Pin_0
  N9: LED1.green_cathode, R3.Pin_0
