# Fritzing sketch activity5 (saved by Fritzing 0.9.1b)
breadboards: 1

parts:
  Part1 = Arduino Uno (Rev3)
  R1 = Resistor [tolerance=±5% resistance=1k package=THT]
  LED1 = smd LED [color="Red (635nm)" package="1206 [SMD]"]
  S2 = Tilt Switch [package=THT]

nets:
  N1: Part1.D11_PWM/MOSI, LED1.anode
  N2: Part1.D2, S2.Pin_1
  N3: Part1.GND, R1.Pin_1, S2.Pin_2
  N4: R1.Pin_0, LED1.cathode
