# Fritzing sketch activity6 (saved by Fritzing 0.8.7b)
breadboards: 1

parts:
  Part1 = Arduino Uno (Rev3)
  J1 = Piezo Speaker
  R1 = Resistor [tolerance=±5% resistance=1k package=THT]
  R2 = TRIMPOT [package=3362u-2]
  R3 = Resistor [tolerance=±5% resistance=10k package=THT]

nets:
  N1: Part1.A0, R2.WIPER
  N2: Part1.D11_PWM/MOSI, J1.pin2
  N3: Part1.5V, R2.CCW
  N4: Part1.GND, R1.Pin_1, R3.Pin_1
  N5: J1.pin1, R1.Pin_0
  N6: R2.CW, R3.Pin_0
