# Fritzing sketch activity7 (saved by Fritzing 0.8.7b)
breadboards: 1

parts:
  Part1 = Arduino Uno (Rev3)
  R3 = Resistor [tolerance=±5% resistance=10k package=THT]
  LED1 = LED - 5mm [color="Red (633nm)" package="5 mm [THT]"]
  R4 = Resistor [tolerance=±5% resistance=1k package=THT]
  R5 = Photocell (LDR) [package=THT]

nets:
  N1: Part1.A0, R3.Pin_0, R5.pin_0
  N2: Part1.D11_PWM/MOSI, LED1.anode
  N3: Part1.5V, R5.pin_1
  N4: Part1.GND, R3.Pin_1, R4.Pin_0
  N5: LED1.cathode, R4.Pin_1
