# Fritzing sketch activity2c (saved by Fritzing 0.9.1b)
breadboards: 1

parts:
  Part1 = Arduino Uno (Rev3)
  R1 = Resistor [tolerance=±5% resistance=1k package=THT]  # not connected
  LED1 = smd LED [color="Red (635nm)" package="1206 [SMD]"]

nets:
  N1: Part1.D11_PWM/MOSI, LED1.anode
