# Fritzing sketch activity5 (saved by Fritzing 0.8.7b)
breadboards: 1

parts:
  Part1 = Arduino Uno (Rev3)
  R1 = Resistor [tolerance=±5% resistance=1k package=THT]
  LED1 = RGB LED (com. anode, rbg) [package="5 mm [THT]"]

nets:
  N1: Part1.D9_PWM, LED1.green_cathode
  N2: Part1.D10_PWM/SS, LED1.common_anode
  N3: Part1.D11_PWM/MOSI, LED1.red_cathode
  N4: Part1.5V, R1.Pin_1
  N5: R1.Pin_0, LED1.blue_cathode
