# Fritzing sketch activity7 (saved by Fritzing 0.8.7b)
breadboards: 1

parts:
  Part1 = Arduino Uno (Rev3)
  R3 = Resistor [tolerance=±5% resistance=10k package=THT]
  J2 = Basic Servo
  R2 = TRIMPOT [package=3386u]

nets:
  N1: Part1.A0, R2.WIPER
  N2: Part1.D11_PWM/MOSI, J2.pulse
  5V: Part1.5V, J2.vcc, R2.CCW
  GND: Part1.GND, R3.Pin_1, J2.gnd
  N3: R3.Pin_0, R2.CW
